# Fritzing sketch Fritzing wiring diagram for Arduino Uno (saved by Fritzing 0.9.2b)

parts:
  Part1 = Arduino Uno (Rev3)  # not connected
  Part2 = Arduino Uno (Rev3)
  Part3 = DeuLigne 1.1 - The Snootlab's LCD shield for Arduino
  Part4 = TRRS 3.5mm Jack Breakout
  Part5 = TRRS 3.5mm Jack Breakout

nets:
  N1: Part2.A0, Part4.TIP
  N2: Part2.GND, Part4.SLEEVE
  N3: Part3.GND, Part5.RING2
  N4: Part3.A0, Part5.TIP

notes:
  Concept 2 3.5mm connection
