# Fritzing sketch nodemcu C2 board (saved by Fritzing 0.9.2b)
breadboards: 1

parts:
  U1 = NodeMCU V1.0
  U2 = 3.5mm Audio Jack [package=audio-jack-3.5mm-smd]
  U3 = LMV358 [package=so08]
  U4 = 3.5mm Audio Jack [package=audio-jack-3.5mm-smd]
  R1 = Resistor [tolerance=±5% resistance=220 package="2512 [SMD]"]

nets:
  N1: U1.3V3, U3.G$1_-IN1, U3.G$1_+V, R1.Pin_0
  N2: U1.GND, U2.SLEEVE, U3.G$1_GND, U4.SLEEVE
  N3: U2.RIGHT, U4.RIGHT
  N4: U2.LEFT, U3.G$1_+IN1, U4.LEFT
  N5: U3.G$1_OUT1, R1.Pin_1

custom parts:
  NodeMCU V1.0: ESP9266 based NodeMCU
