# Fritzing sketch nodemcu reed switch boardfzz (saved by Fritzing 0.9.2b)
breadboards: 1

parts:
  U1 = NodeMCU V1.0
  S1 = SWITCH-MOMENTARY-2 [package=reed_switch_pth]
  U2 = AUDIO-JACK2 [package=audio-jack]

nets:
  N1: U1.D2, U2.TIP
  N2: U1.GND, S1.1, U2.SLEEVE

notes:
  Reed switch senses rotations of flywheel - most rowing machines already have this to sense movement.
  3.5mm Jack connection is common to many rowing machines

custom parts:
  NodeMCU V1.0: ESP9266 based NodeMCU
